# Fritzing sketch mastermind_schema_PCB_v0.3 (saved by Fritzing 0.9.2b)
circuit board: 6.53cm x 14.3221cm
breadboards: 1

parts:
  74HC156-1 = 74HC165 [part_number=74HC165 package="DIP (Dual Inline) [THT]"]
  75HC595-1 = 74HC595 [package="DIP16 [THT]"]
  75HC595-3 = 74HC595 [package="DIP16 [THT]"]
  75HC595-4 = 74HC595 [package="DIP16 [THT]"]
  J100 = Piezo Speaker
  S4 = Pushbutton [package="[THT]"]
  S3 = Pushbutton [package="[THT]"]
  S2 = Pushbutton [package="[THT]"]
  S1 = Pushbutton [package="[THT]"]
  S5 = Pushbutton [package="[THT]"]
  J102 = female pin header, 3 pins [form="♀ (female)"]
  J103 = female pin header, 3 pins [form="♀ (female)"]
  J104 = female pin header, 3 pins [form="♀ (female)"]
  J105 = female pin header, 3 pins [form="♀ (female)"]
  J106 = female pin header, 3 pins [form="♀ (female)"]
  J107 = female pin header, 3 pins [form="♀ (female)"]
  J108 = female pin header, 3 pins [form="♀ (female)"]
  J109 = female pin header, 3 pins [form="♀ (female)"]
  Q26 = PNP-Transistor [package="TO92 [THT]"]
  LED116 = RGB LED (com. anode, rbg) [package="5 mm [THT]"]
  LED117 = RGB LED (com. anode, rbg) [package="5 mm [THT]"]
  LED118 = RGB LED (com. anode, rbg) [package="5 mm [THT]"]
  LED119 = RGB LED (com. anode, rbg) [package="5 mm [THT]"]
  LED120 = RGB LED (com. anode, rbg) [package="5 mm [THT]"]
  LED121 = RGB LED (com. anode, rbg) [package="5 mm [THT]"]
  LED122 = RGB LED (com. anode, rbg) [package="5 mm [THT]"]
  LED123 = RGB LED (com. anode, rbg) [package="5 mm [THT]"]
  Q27 = PNP-Transistor [package="TO92 [THT]"]
  J110 = female pin header, 3 pins [form="♀ (female)"]
  J111 = female pin header, 3 pins [form="♀ (female)"]
  J112 = female pin header, 3 pins [form="♀ (female)"]
  J113 = female pin header, 3 pins [form="♀ (female)"]
  J114 = female pin header, 3 pins [form="♀ (female)"]
  J115 = female pin header, 3 pins [form="♀ (female)"]
  J116 = female pin header, 3 pins [form="♀ (female)"]
  J117 = female pin header, 3 pins [form="♀ (female)"]
  Q28 = PNP-Transistor [package="TO92 [THT]"]
  LED124 = RGB LED (com. anode, rbg) [package="5 mm [THT]"]
  LED125 = RGB LED (com. anode, rbg) [package="5 mm [THT]"]
  LED126 = RGB LED (com. anode, rbg) [package="5 mm [THT]"]
  LED127 = RGB LED (com. anode, rbg) [package="5 mm [THT]"]
  LED128 = RGB LED (com. anode, rbg) [package="5 mm [THT]"]
  LED129 = RGB LED (com. anode, rbg) [package="5 mm [THT]"]
  LED130 = RGB LED (com. anode, rbg) [package="5 mm [THT]"]
  LED131 = RGB LED (com. anode, rbg) [package="5 mm [THT]"]
  Q29 = PNP-Transistor [package="TO92 [THT]"]
  Q30 = PNP-Transistor [package="TO92 [THT]"]
  J118 = female pin header, 3 pins [form="♀ (female)"]
  J119 = female pin header, 3 pins [form="♀ (female)"]
  J120 = female pin header, 3 pins [form="♀ (female)"]
  J121 = female pin header, 3 pins [form="♀ (female)"]
  J122 = female pin header, 3 pins [form="♀ (female)"]
  J123 = female pin header, 3 pins [form="♀ (female)"]
  J124 = female pin header, 3 pins [form="♀ (female)"]
  J125 = female pin header, 3 pins [form="♀ (female)"]
  Q31 = PNP-Transistor [package="TO92 [THT]"]
  LED132 = RGB LED (com. anode, rbg) [package="5 mm [THT]"]
  LED133 = RGB LED (com. anode, rbg) [package="5 mm [THT]"]
  LED134 = RGB LED (com. anode, rbg) [package="5 mm [THT]"]
  LED135 = RGB LED (com. anode, rbg) [package="5 mm [THT]"]
  LED136 = RGB LED (com. anode, rbg) [package="5 mm [THT]"]
  LED137 = RGB LED (com. anode, rbg) [package="5 mm [THT]"]
  LED138 = RGB LED (com. anode, rbg) [package="5 mm [THT]"]
  LED139 = RGB LED (com. anode, rbg) [package="5 mm [THT]"]
  Q32 = PNP-Transistor [package="TO92 [THT]"]
  Q33 = PNP-Transistor [package="TO92 [THT]"]
  J126 = female pin header, 3 pins [form="♀ (female)"]
  J127 = female pin header, 3 pins [form="♀ (female)"]
  J128 = female pin header, 3 pins [form="♀ (female)"]
  J129 = female pin header, 3 pins [form="♀ (female)"]
  J130 = female pin header, 3 pins [form="♀ (female)"]
  J131 = female pin header, 3 pins [form="♀ (female)"]
  J132 = female pin header, 3 pins [form="♀ (female)"]
  J133 = female pin header, 3 pins [form="♀ (female)"]
  Q34 = PNP-Transistor [package="TO92 [THT]"]
  LED140 = RGB LED (com. anode, rbg) [package="5 mm [THT]"]
  LED141 = RGB LED (com. anode, rbg) [package="5 mm [THT]"]
  LED142 = RGB LED (com. anode, rbg) [package="5 mm [THT]"]
  LED143 = RGB LED (com. anode, rbg) [package="5 mm [THT]"]
  LED144 = RGB LED (com. anode, rbg) [package="5 mm [THT]"]
  LED145 = RGB LED (com. anode, rbg) [package="5 mm [THT]"]
  LED146 = RGB LED (com. anode, rbg) [package="5 mm [THT]"]
  LED147 = RGB LED (com. anode, rbg) [package="5 mm [THT]"]
  J134 = female pin header, 3 pins [form="♀ (female)"]
  J135 = female pin header, 3 pins [form="♀ (female)"]
  J136 = female pin header, 3 pins [form="♀ (female)"]
  J137 = female pin header, 3 pins [form="♀ (female)"]
  J138 = female pin header, 3 pins [form="♀ (female)"]
  J139 = female pin header, 3 pins [form="♀ (female)"]
  J140 = female pin header, 3 pins [form="♀ (female)"]
  J141 = female pin header, 3 pins [form="♀ (female)"]
  Q35 = PNP-Transistor [package="TO92 [THT]"]
  LED148 = RGB LED (com. anode, rbg) [package="5 mm [THT]"]
  LED149 = RGB LED (com. anode, rbg) [package="5 mm [THT]"]
  LED150 = RGB LED (com. anode, rbg) [package="5 mm [THT]"]
  LED151 = RGB LED (com. anode, rbg) [package="5 mm [THT]"]
  LED152 = RGB LED (com. anode, rbg) [package="5 mm [THT]"]
  LED153 = RGB LED (com. anode, rbg) [package="5 mm [THT]"]
  LED154 = RGB LED (com. anode, rbg) [package="5 mm [THT]"]
  LED155 = RGB LED (com. anode, rbg) [package="5 mm [THT]"]
  C15 = Ceramic Capacitor [capacitance=100nF package="100 mil [THT, multilayer]"]
  C16 = Ceramic Capacitor [capacitance=100nF package="100 mil [THT, multilayer]"]
  R145 = Resistor [tolerance=±5% resistance=220 package=THT]
  R144 = Resistor [tolerance=±5% resistance=220 package=THT]
  R146 = Resistor [tolerance=±5% resistance=220 package=THT]
  R147 = Resistor [tolerance=±5% resistance=220 package=THT]
  R148 = Resistor [tolerance=±5% resistance=220 package=THT]
  R149 = Resistor [tolerance=±5% resistance=220 package=THT]
  R150 = Resistor [tolerance=±5% resistance=220 package=THT]
  R151 = Resistor [tolerance=±5% resistance=220 package=THT]
  S9 = Pushbutton [package="[THT]"]
  S10 = Pushbutton [package="[THT]"]
  S11 = Pushbutton [package="[THT]"]
  C18 = Ceramic Capacitor [capacitance=100nF package="100 mil [THT, multilayer]"]
  R152 = Resistor [tolerance=±5% resistance=220 package=THT]
  R153 = Resistor [tolerance=±5% resistance=220 package=THT]
  R154 = Resistor [tolerance=±5% resistance=220 package=THT]
  R155 = Resistor [tolerance=±5% resistance=220 package=THT]
  R156 = Resistor [tolerance=±5% resistance=220 package=THT]
  R157 = Resistor [tolerance=±5% resistance=220 package=THT]
  R158 = Resistor [tolerance=±5% resistance=220 package=THT]
  R160 = Resistor [tolerance=±5% resistance=220 package=THT]
  R161 = Resistor [tolerance=±5% resistance=220 package=THT]
  R162 = Resistor [tolerance=±5% resistance=220 package=THT]
  R163 = Resistor [tolerance=±5% resistance=220 package=THT]
  R164 = Resistor [tolerance=±5% resistance=220 package=THT]
  R165 = Resistor [tolerance=±5% resistance=220 package=THT]
  R166 = Resistor [tolerance=±5% resistance=220 package=THT]
  R167 = Resistor [tolerance=±5% resistance=220 package=THT]
  R168 = Resistor [tolerance=±5% resistance=220 package=THT]
  R169 = Resistor [tolerance=±5% resistance=220 package=THT]
  R170 = Resistor [tolerance=±5% resistance=220 package=THT]
  R171 = Resistor [tolerance=±5% resistance=220 package=THT]
  R172 = Resistor [tolerance=±5% resistance=220 package=THT]
  R173 = Resistor [tolerance=±5% resistance=220 package=THT]
  R174 = Resistor [tolerance=±5% resistance=220 package=THT]
  R175 = Resistor [tolerance=±5% resistance=220 package=THT]
  R176 = Resistor [tolerance=±5% resistance=220 package=THT]
  C22 = Ceramic Capacitor [capacitance=100nF package="100 mil [THT, multilayer]"]
  J142 = AVR ISP 6 Pin [package=2x3]
  C23 = Ceramic Capacitor [capacitance=100nF package="100 mil [THT, multilayer]"]
  atmega328-1 = atmega328 [package=dip]
  R177 = Resistor [tolerance=±5% resistance=220 package=THT]
  R178 = Resistor [tolerance=±5% resistance=220 package=THT]
  R183 = Resistor [tolerance=±5% resistance=220 package=THT]
  C24 = Ceramic Capacitor [capacitance=100nF package="100 mil [THT, multilayer]"]
  R194 = Resistor [tolerance=±5% resistance=220 package=THT]
  R195 = Resistor [tolerance=±5% resistance=220 package=THT]
  R197 = Resistor [tolerance=±5% resistance=220 package=THT]
  R198 = Resistor [tolerance=±5% resistance=220 package=THT]
  R199 = Resistor [tolerance=±5% resistance=100 package=THT]
  C14 = Ceramic Capacitor [capacitance=22nF package="100 mil [THT, multilayer]"]
  C20 = Ceramic Capacitor [capacitance=22nF package="100 mil [THT, multilayer]"]
  XTAL1 = Crystal [frequency="16 Mhz" package=THT]
  C25 = Ceramic Capacitor [capacitance=100nF package="100 mil [THT, multilayer]"]
  R200 = Resistor [tolerance=±5% resistance=220 package=THT]
  VCC1 = Battery
  C26 = Electrolytic Capacitor [capacitance=47µF package="100 mil [THT, electrolytic]"]
  C27 = Electrolytic Capacitor [capacitance=47µF package="100 mil [THT, electrolytic]"]
  S12 = SPST Switch [package=switch-spdt]
  R201 = Resistor [tolerance=±5% resistance=1k package=THT]
  LED156 = LED - 3mm [color="Red (633nm)" package="3 mm [THT]"]
  75HC595-2 = 74HC595 [package="DIP16 [THT]"]

nets:
  N1: 74HC156-1.!PL, atmega328-1.D7
  N2: 74HC156-1.CP, atmega328-1.D6_(PWM)
  N3: 74HC156-1.D4, S10.Pin_1, S10.Pin_2, R198.Pin_1
  N4: 74HC156-1.D5, S1.Pin_1, S1.Pin_2, R178.Pin_1
  N5: 74HC156-1.D6, S11.Pin_1, S11.Pin_2, R177.Pin_0
  N6: 74HC156-1.D7, S5.Pin_3, S5.Pin_4, R200.Pin_0
  GND: 74HC156-1.GND, 74HC156-1.DS, 74HC156-1.!CE, 75HC595-1.GND, 75HC595-1.OE, 75HC595-3.GND, 75HC595-3.OE, 75HC595-4.GND, 75HC595-4.OE, C15.0, C16.1, C18.1, C22.1, J142.6, C23.0, atmega328-1.GND, R177.Pin_1, R178.Pin_0, R183.Pin_0, C24.0, R194.Pin_0, R195.Pin_1, R197.Pin_0, R198.Pin_0, C14.1, C20.0, C25.0, R200.Pin_1, VCC1.-, C26.-, C27.-, R201.Pin_1, 75HC595-2.GND, 75HC595-2.OE
  N7: 74HC156-1.Q7, atmega328-1.D5_(PWM)
  N8: 74HC156-1.D0, S4.Pin_1, S4.Pin_2, R194.Pin_1
  N9: 74HC156-1.D1, S3.Pin_1, S3.Pin_2, R195.Pin_0
  N10: 74HC156-1.D2, S2.Pin_1, S2.Pin_2, R183.Pin_1
  N11: 74HC156-1.D3, S9.Pin_1, S9.Pin_2, R197.Pin_1
  VCC: 74HC156-1.Vcc, 75HC595-1.MR, 75HC595-1.VCC, 75HC595-3.MR, 75HC595-3.VCC, 75HC595-4.MR, 75HC595-4.VCC, S4.Pin_3, S4.Pin_4, S3.Pin_3, S3.Pin_4, S2.Pin_3, S2.Pin_4, S1.Pin_3, S5.Pin_1, Q26.E, Q27.E, Q28.E, Q29.E, Q30.E, Q31.E, Q32.E, Q33.E, Q34.E, Q35.E, C15.1, C16.0, S9.Pin_3, S9.Pin_4, S10.Pin_3, S10.Pin_4, S11.Pin_3, S11.Pin_4, C18.0, C22.0, C23.1, atmega328-1.VCC, atmega328-1.AVCC, atmega328-1.AREF, C24.1, C25.1, C26.+, C27.+, S12.P, LED156.anode, 75HC595-2.MR, 75HC595-2.VCC
  N12: 75HC595-1.Q1, R173.Pin_0
  N13: 75HC595-1.Q2, R174.Pin_1
  N14: 75HC595-1.Q3, R171.Pin_0
  N15: 75HC595-1.Q4, R169.Pin_1
  N16: 75HC595-1.Q5, R172.Pin_0
  N17: 75HC595-1.Q6, R170.Pin_1
  N18: 75HC595-1.Q7, R176.Pin_0
  N19: 75HC595-1.Q7', 75HC595-2.DS
  N20: 75HC595-1.SH_CP, 75HC595-3.SH_CP, 75HC595-4.SH_CP, atmega328-1.D3_(PWM), 75HC595-2.SH_CP
  N21: 75HC595-1.ST_CP, 75HC595-3.ST_CP, 75HC595-4.ST_CP, atmega328-1.D2, 75HC595-2.ST_CP
  N22: 75HC595-1.DS, atmega328-1.D4
  N23: 75HC595-1.Q0, R175.Pin_0
  N24: 75HC595-3.Q1, R156.Pin_0
  N25: 75HC595-3.Q2, R157.Pin_1
  N26: 75HC595-3.Q3, R154.Pin_0
  N27: 75HC595-3.Q4, R152.Pin_1
  N28: 75HC595-3.Q5, R155.Pin_0
  N29: 75HC595-3.Q6, R153.Pin_1
  N30: 75HC595-3.Q7, R160.Pin_0
  N31: 75HC595-3.Q7', 75HC595-4.DS
  N32: 75HC595-3.DS, 75HC595-2.Q7'
  N33: 75HC595-3.Q0, R158.Pin_1
  N34: 75HC595-4.Q1, R144.Pin_1
  N35: 75HC595-4.Q2, R147.Pin_0
  N36: 75HC595-4.Q3, R146.Pin_1
  N37: 75HC595-4.Q4, R149.Pin_0
  N38: 75HC595-4.Q5, R151.Pin_1
  N39: 75HC595-4.Q6, R148.Pin_0
  N40: 75HC595-4.Q7, R150.Pin_1
  N41: 75HC595-4.Q0, R145.Pin_0
  N42: J100.pin1, R199.Pin_1
  N43: J100.pin2, atmega328-1.D10_(PWM)
  N44: J102.pin1, J107.pin1, J110.pin1, J115.pin1, J118.pin1, J123.pin1, J126.pin1, J131.pin1, J134.pin1, J139.pin1, R154.Pin_1
  N45: J102.pin2, J103.pin2, J104.pin2, J105.pin2, LED119.common_anode, LED120.common_anode, LED122.common_anode, LED123.common_anode, Q27.C
  N46: J102.pin3, J107.pin3, J110.pin3, J115.pin3, J118.pin3, J123.pin3, J126.pin3, J131.pin3, J134.pin3, J139.pin3, R148.Pin_1
  N47: J103.pin1, J106.pin1, J111.pin1, J114.pin1, J119.pin1, J122.pin1, J127.pin1, J130.pin1, J135.pin1, J138.pin1, R152.Pin_0
  N48: J103.pin3, J106.pin3, J111.pin3, J114.pin3, J119.pin3, J122.pin3, J127.pin3, J130.pin3, J135.pin3, J138.pin3, R164.Pin_1
  N49: J104.pin1, J108.pin1, J112.pin1, J116.pin1, J120.pin1, J124.pin1, J128.pin1, J132.pin1, J136.pin1, J140.pin1, R157.Pin_0
  N50: J104.pin3, J108.pin3, J112.pin3, J116.pin3, J120.pin3, J124.pin3, J128.pin3, J132.pin3, J136.pin3, J140.pin3, R150.Pin_0
  N51: J105.pin1, J109.pin1, J113.pin1, J117.pin1, J121.pin1, J125.pin1, J129.pin1, J133.pin1, J137.pin1, J141.pin1, R160.Pin_1
  N52: J105.pin3, J109.pin3, J113.pin3, J117.pin3, J121.pin3, J125.pin3, J129.pin3, J133.pin3, J137.pin3, J141.pin3, R161.Pin_0
  N53: J106.pin2, J107.pin2, J108.pin2, J109.pin2, Q26.C, LED116.common_anode, LED117.common_anode, LED118.common_anode, LED121.common_anode
  N54: Q26.B, R169.Pin_0
  N55: LED116.red_cathode, LED122.red_cathode, LED124.red_cathode, LED130.red_cathode, LED132.red_cathode, LED138.red_cathode, LED140.red_cathode, LED146.red_cathode, LED148.red_cathode, LED154.red_cathode, R167.Pin_0
  N56: LED116.blue_cathode, LED122.blue_cathode, LED124.blue_cathode, LED130.blue_cathode, LED132.blue_cathode, LED138.blue_cathode, LED140.blue_cathode, LED146.blue_cathode, LED148.blue_cathode, LED154.blue_cathode, R163.Pin_1
  N57: LED116.green_cathode, LED122.green_cathode, LED124.green_cathode, LED130.green_cathode, LED132.green_cathode, LED138.green_cathode, LED140.green_cathode, LED146.green_cathode, LED148.green_cathode, LED154.green_cathode, R168.Pin_1
  N58: LED117.red_cathode, LED123.red_cathode, LED125.red_cathode, LED131.red_cathode, LED133.red_cathode, LED139.red_cathode, LED141.red_cathode, LED147.red_cathode, LED149.red_cathode, LED155.red_cathode, R149.Pin_1
  N59: LED117.blue_cathode, LED123.blue_cathode, LED125.blue_cathode, LED131.blue_cathode, LED133.blue_cathode, LED139.blue_cathode, LED141.blue_cathode, LED147.blue_cathode, LED149.blue_cathode, LED155.blue_cathode, R156.Pin_1
  N60: LED117.green_cathode, LED123.green_cathode, LED125.green_cathode, LED131.green_cathode, LED133.green_cathode, LED139.green_cathode, LED141.green_cathode, LED147.green_cathode, LED149.green_cathode, LED155.green_cathode, R155.Pin_1
  N61: LED118.red_cathode, LED120.red_cathode, LED126.red_cathode, R173.Pin_1
  N62: LED118.blue_cathode, LED120.blue_cathode, LED126.blue_cathode, LED128.blue_cathode, LED134.blue_cathode, LED136.blue_cathode, LED142.blue_cathode, LED144.blue_cathode, LED150.blue_cathode, LED152.blue_cathode, R171.Pin_1
  N63: LED118.green_cathode, LED120.green_cathode, LED126.green_cathode, LED128.green_cathode, LED134.green_cathode, LED136.green_cathode, LED142.green_cathode, LED144.green_cathode, LED150.green_cathode, LED152.green_cathode, R172.Pin_1
  N64: LED119.red_cathode, LED121.red_cathode, LED127.red_cathode, LED129.red_cathode, LED135.red_cathode, LED137.red_cathode, LED143.red_cathode, LED145.red_cathode, LED151.red_cathode, LED153.red_cathode, R145.Pin_1
  N65: LED119.blue_cathode, LED121.blue_cathode, LED127.blue_cathode, LED129.blue_cathode, LED135.blue_cathode, LED137.blue_cathode, LED143.blue_cathode, LED145.blue_cathode, LED151.blue_cathode, LED153.blue_cathode, R144.Pin_0
  N66: LED119.green_cathode, LED121.green_cathode, LED127.green_cathode, LED129.green_cathode, LED135.green_cathode, LED137.green_cathode, LED143.green_cathode, LED145.green_cathode, LED151.green_cathode, LED153.green_cathode, R146.Pin_0
  N67: Q27.B, R174.Pin_0
  N68: J110.pin2, J111.pin2, J112.pin2, J113.pin2, LED127.common_anode, LED128.common_anode, LED130.common_anode, LED131.common_anode, Q29.C
  N69: J114.pin2, J115.pin2, J116.pin2, J117.pin2, Q28.C, LED124.common_anode, LED125.common_anode, LED126.common_anode, LED129.common_anode
  N70: Q28.B, R175.Pin_1
  N71: LED128.red_cathode, LED134.red_cathode, LED136.red_cathode, LED142.red_cathode, LED144.red_cathode, LED150.red_cathode, LED152.red_cathode
  N72: Q29.B, R162.Pin_0
  N73: Q30.B, R165.Pin_1
  N74: Q30.C, J118.pin2, J119.pin2, J120.pin2, J121.pin2, LED135.common_anode, LED136.common_anode, LED138.common_anode, LED139.common_anode
  N75: J122.pin2, J123.pin2, J124.pin2, J125.pin2, Q31.C, LED132.common_anode, LED133.common_anode, LED134.common_anode, LED137.common_anode
  N76: Q31.B, R166.Pin_0
  N77: Q32.B, R147.Pin_1
  N78: Q32.C, J126.pin2, J127.pin2, J128.pin2, J129.pin2, LED143.common_anode, LED144.common_anode, LED146.common_anode, LED147.common_anode
  N79: Q33.B, R158.Pin_0
  N80: Q33.C, J134.pin2, J135.pin2, J136.pin2, J137.pin2, LED151.common_anode, LED152.common_anode, LED154.common_anode, LED155.common_anode
  N81: J130.pin2, J131.pin2, J132.pin2, J133.pin2, Q34.C, LED140.common_anode, LED141.common_anode, LED142.common_anode, LED145.common_anode
  N82: Q34.B, R151.Pin_0
  N83: J138.pin2, J139.pin2, J140.pin2, J141.pin2, Q35.C, LED148.common_anode, LED149.common_anode, LED150.common_anode, LED153.common_anode
  N84: Q35.B, R153.Pin_0
  N85: R161.Pin_1, 75HC595-2.Q4
  N86: R162.Pin_1, 75HC595-2.Q6
  N87: R163.Pin_0, 75HC595-2.Q3
  N88: R164.Pin_0, 75HC595-2.Q5
  N89: R165.Pin_0, 75HC595-2.Q1
  N90: R166.Pin_1, 75HC595-2.Q2
  N91: R167.Pin_1, 75HC595-2.Q0
  N92: R168.Pin_0, 75HC595-2.Q7
  N93: J142.1, atmega328-1.D12
  N94: J142.3, atmega328-1.D13
  N95: J142.4, atmega328-1.D11_(PWM)
  N96: J142.5, atmega328-1.RESET
  N97: atmega328-1.XLAT1, C20.1, XTAL1.pin_1
  N98: atmega328-1.XLAT2, C14.0, XTAL1.pin_0
  N99: atmega328-1.D9_(PWM), R199.Pin_0
  N100: VCC1.+, S12.S
  N101: R201.Pin_0, LED156.cathode

notes:
  Mastermind v0.2
  by Claudio & Pierre-Frederic

custom parts:
  74HC165: Asynchrounous parallel-in serial-out.
